# Fritzing sketch Audio Circuit Step 1 (saved by Fritzing 0.9.3b)
perfboards: 1

parts:
  U1 = attiny85 [package=dip]
  Q1 = pnp-Powertransistor [package="TO220 [THT]"]
  R1 = Resistor [tolerance=±5% resistance=1k package=THT]
  VCC2 = 4 x AAA Battery Mount  # not connected
  VCC3 = Battery block 9V

nets:
  N1: U1.Pin_4, Q1.emitter, VCC3.-
  N2: U1.Pin_5, R1.Pin_1

notes:
  It is best to run the ground "rail" underneath the wires on the spider, and the power (+5V) rail on the outside
  Connect the power supply here (+5V or +4.5V from 3 AAA batteries)
  Run the power and ground rails around the spider for easy access
  Connect the speaker power supply here (+9V using the connector)
