# Fritzing sketch Audio Circuit Step 2 (saved by Fritzing 0.9.3b)
perfboards: 1

parts:
  U1 = attiny85 [package=dip]
  Q1 = pnp-Powertransistor [package="TO220 [THT]"]
  R1 = Resistor [tolerance=±5% resistance=1k package=THT]
  VCC2 = 4 x AAA Battery Mount  # not connected
  VCC3 = Battery block 9V
  SP1 = SPEAKER [package=pcb_mount_speaker]

nets:
  N1: U1.Pin_4, Q1.emitter, VCC3.-
  N2: U1.Pin_5, R1.Pin_1
  N3: Q1.collector, SP1.+

notes:
  Attach a speaker to the speaker +9V and GND (this can be a paper speaker or any type)
