# Fritzing sketch Basic Circuit Step 3 (saved by Fritzing 0.9.3b)
perfboards: 1

parts:
  U1 = attiny85 [package=dip]
  VCC1 = 4 x AAA Battery Mount  # not connected
  LED1 = LED - 5mm [color="Red (633nm)" package="5 mm [THT]"]
  LED2 = LED - 5mm [color="Red (633nm)" package="5 mm [THT]"]
  LED3 = LED - 5mm [color="Red (633nm)" package="5 mm [THT]"]
  S1 = Pushbutton [package="[THT]"]  # not connected
  S2 = Toggle Switch [package=THT]  # not connected
  R1 = Resistor [tolerance=±5% resistance=220 package=THT]  # not connected

nets:
  N1: U1.Pin_5, LED3.anode
  N2: U1.Pin_6, LED2.anode
  N3: U1.Pin_7, LED1.anode

notes:
  OR
  Attach some kind of switch from pin 4 to the +5V strip - it can be any kind of button, toggle or switch
  (The input you get may be less sporatic if you add a "pull-down resistor" going from the pin to ground)
  OPTIONAL
  Alternatively (to avoid resistors) you can add two strips, one going to GND and the other to +5V, and touch one for on and one for off.
